# Fritzing sketch rpi_sketch (saved by Fritzing 0.9.4)

parts:
  Raspberry_Pi_4B = Raspberry Pi 4B
  Raspberry_Pi_Sense_Hat1 = Raspberry Pi Sense Hat

nets:
  3V3: Raspberry_Pi_4B.3V3, Raspberry_Pi_Sense_Hat1.3v3
  5V: Raspberry_Pi_4B.5V, Raspberry_Pi_Sense_Hat1.5V
  N1: Raspberry_Pi_4B.GPIO2, Raspberry_Pi_Sense_Hat1.GPIO2
  N2: Raspberry_Pi_4B.GPIO3, Raspberry_Pi_Sense_Hat1.GPIO3
  GND: Raspberry_Pi_4B.GND, Raspberry_Pi_Sense_Hat1.GND
  N3: Raspberry_Pi_4B.GPIO23, Raspberry_Pi_Sense_Hat1.GIPO23
  N4: Raspberry_Pi_4B.GPIO24, Raspberry_Pi_Sense_Hat1.GIPO24
  N5: Raspberry_Pi_4B.ID_SD, Raspberry_Pi_Sense_Hat1.ID_SD
  N6: Raspberry_Pi_4B.ID_SC, Raspberry_Pi_Sense_Hat1.ID_SC

custom parts:
  Raspberry Pi Sense Hat: The Sense HAT is an add-on board for Raspberry Pi, made especially for the Astro Pi mission – it launched to the International Space Station in December 2015. The Sense HAT has an 8×8 RGB LED matrix, a five-button joystick and includes the following sensors: Gyroscope Accelerometer Magnetometer Temperature Barometric pressure Humidity
